# Fritzing sketch Tortoise-heat-control  (saved by Fritzing 0.9.3b)
stripboards: 1

parts:
  WeMos_D1_Mini1 = WeMos D1 Mini  # not connected
  Q1 = NPN-Transistor [package="TO92 [THT]"]
  R1 = Resistor [tolerance=±5% resistance=3.3k package=THT]
  R2 = Resistor [tolerance=±5% resistance=4.7k package=THT]
  Part1 = KY-019 5V Relay Module [package="Breakout board"]
  J1 = screw terminal, 3 pins
  DS1 = DS18B20 1-Wire Temperature Sensor [part_number=DS18B20]
  R3 = Resistor [tolerance=±5% resistance=4.7 package=THT]
  LED1 = LED - 5mm [color="Green (570nm)" package="5 mm [THT]"]
  LED2 = LED - 5mm [color="Red (633nm)" package="5 mm [THT]"]
  DS2 = DS18B20 1-Wire Temperature Sensor [part_number=DS18B20]
  DS3 = DS18B20 1-Wire Temperature Sensor [part_number=DS18B20]
  R4 = Resistor [tolerance=±5% resistance=4.7 package=THT]

nets (from the breadboard view):
  N1: Q1.E, Part1.+
  N2: Q1.B, R1.Pin_1
  GND: Q1.C, R2.Pin_0, Part1.S, J1.pin1, DS1.GND, DS2.GND, DS3.GND, R4.Pin_1
  N3: R2.Pin_1, J1.pin2, DS1.DQ, DS2.DQ, DS3.DQ
  VDD: Part1.-, J1.pin3, DS1.VDD, LED1.anode, LED2.anode, DS2.VDD, DS3.VDD
  N4: R3.Pin_0, LED1.cathode
  N5: LED2.cathode, R4.Pin_0

notes:
  From 240 v LIVE
  Live to heater
  Tree DS18B20 waterproof sensors
  Power ON/OFF LED
  Heater ON/OFF LED

custom parts:
  KY-019 5V Relay Module: KY-019 5V Relay module, used to control AC circuits.
